// Digital circuit 3StateBuf.dig as structural Verilog
module _3StateBuf (
  input  [7:0] IN,
  input  EN,
  output [7:0] OUT
);

  wire not_1_out;

  not not_1 (not_1_out, EN);
  _74244 _74244_1 (
    .pin1(not_1_out), .pin2(IN[0]), .pin3(OUT[7]), .pin4(IN[1]), .pin5(OUT[6]), .pin6(IN[2]), .pin7(OUT[5]),
    .pin8(IN[3]), .pin9(OUT[4]), .pin10(1'b0), .pin11(IN[4]), .pin12(OUT[3]), .pin13(IN[5]), .pin14(OUT[2]),
    .pin15(IN[6]), .pin16(OUT[1]), .pin17(IN[7]), .pin18(OUT[0]), .pin19(not_1_out), .pin20(1'b1));
endmodule
