// Digital circuit AdderSubtracter.dig as structural Verilog
module AdderSubtracter (
  input  [7:0] A,
  input  [7:0] B,
  input  SUB,
  input  EN,
  output [7:0] S
);

  wire _74283_1_pin9, not_2_out;
  wire [3:0] _74283_1_pin1, _74283_2_pin1;
  wire [7:0] multiplexer_1_out, not_1_out;

  Multiplexer #(.Bits(8)) multiplexer_1 (.sel(SUB), .in_0(B), .in_1(not_1_out), .out(multiplexer_1_out));
  assign not_1_out = ~B;  // Not not_1, 8 bits wide
  _74283 _74283_1 (
    .pin1(_74283_1_pin1[1]), .pin2(multiplexer_1_out[1]), .pin3(A[1]), .pin4(_74283_1_pin1[0]), .pin5(A[0]),
    .pin6(multiplexer_1_out[0]), .pin7(SUB), .pin8(1'b0), .pin9(_74283_1_pin9), .pin10(_74283_1_pin1[3]),
    .pin11(multiplexer_1_out[3]), .pin12(A[3]), .pin13(_74283_1_pin1[2]), .pin14(A[2]),
    .pin15(multiplexer_1_out[2]), .pin16(1'b1));
  _74283 _74283_2 (
    .pin1(_74283_2_pin1[1]), .pin2(multiplexer_1_out[5]), .pin3(A[5]), .pin4(_74283_2_pin1[0]), .pin5(A[4]),
    .pin6(multiplexer_1_out[4]), .pin7(_74283_1_pin9), .pin8(1'b0), .pin10(_74283_2_pin1[3]),
    .pin11(multiplexer_1_out[7]), .pin12(A[7]), .pin13(_74283_2_pin1[2]), .pin14(A[6]),
    .pin15(multiplexer_1_out[6]), .pin16(1'b1));  // open: pin9
  not not_2 (not_2_out, EN);
  _74244 _74244_1 (
    .pin1(not_2_out), .pin2(_74283_1_pin1[0]), .pin3(S[7]), .pin4(_74283_1_pin1[1]), .pin5(S[6]),
    .pin6(_74283_1_pin1[2]), .pin7(S[5]), .pin8(_74283_1_pin1[3]), .pin9(S[4]), .pin10(1'b0),
    .pin11(_74283_2_pin1[0]), .pin12(S[3]), .pin13(_74283_2_pin1[1]), .pin14(S[2]), .pin15(_74283_2_pin1[2]),
    .pin16(S[1]), .pin17(_74283_2_pin1[3]), .pin18(S[0]), .pin19(not_2_out), .pin20(1'b1));
endmodule
