// Digital circuit EqualsZero.dig as structural Verilog
module EqualsZero (
  input  [7:0] IN,
  output OUT
);

  wire xnor_1_out, xnor_2_out, xnor_3_out, xnor_4_out, xnor_5_out, xnor_6_out, xnor_7_out, xnor_8_out;

  xnor xnor_1 (xnor_1_out, IN[0], 1'b0);
  xnor xnor_2 (xnor_2_out, IN[1], 1'b0);
  xnor xnor_3 (xnor_3_out, IN[2], 1'b0);
  xnor xnor_4 (xnor_4_out, IN[3], 1'b0);
  xnor xnor_5 (xnor_5_out, IN[4], 1'b0);
  xnor xnor_6 (xnor_6_out, IN[5], 1'b0);
  xnor xnor_7 (xnor_7_out, IN[6], 1'b0);
  xnor xnor_8 (xnor_8_out, IN[7], 1'b0);
  and and_1 (OUT, xnor_1_out, xnor_2_out, xnor_3_out, xnor_4_out, xnor_5_out, xnor_6_out, xnor_7_out, xnor_8_out);
endmodule
