// Digital circuit Kontrol.dig as structural Verilog
module Kontrol (
  input  [3:0] OP,
  input  [1:0] RX,
  input  [1:0] RY,
  input  [7:0] ADR,
  input  EZ,
  output MR,
  output MW,
  output [1:0] RS,
  output [1:0] WS,
  output [1:0] AA,
  output [1:0] AB,
  output AS,
  output AW,
  output [7:0] D,
  output DE,
  output CE,
  output [3:0] AD,
  output CO,
  output RR,
  output RW
);

  wire and_1_out, decoder_1_out_0, decoder_1_out_3, decoder_1_out_4, decoder_1_out_5, decoder_1_out_6,
       not_1_out;
  wire [3:0] delay_1_out;

  Delay #(.Bits(4), .delayTime(2)) delay_1 (.in(OP), .out(delay_1_out));
  Decoder #(.Selector_Bits(4)) decoder_1 (
    .sel(delay_1_out), .out_0(decoder_1_out_0), .out_1(AS), .out_2(DE), .out_3(decoder_1_out_3),
    .out_4(decoder_1_out_4), .out_5(decoder_1_out_5), .out_6(decoder_1_out_6), .out_7(RR), .out_8(RW));  // open: out_9, out_10, out_11, out_12, out_13, out_14, out_15
  not not_1 (not_1_out, EZ);
  and and_1 (and_1_out, decoder_1_out_5, not_1_out);
  or or_1 (CO, decoder_1_out_4, and_1_out);
  not not_2 (CE, decoder_1_out_6);
  or or_2 (MR, decoder_1_out_0, AS, DE, decoder_1_out_3, RW);
  or or_3 (MW, decoder_1_out_3, RR);
  or or_4 (AW, AS, decoder_1_out_0);

  assign AA = RX;
  assign AB = RY;
  assign AD = ADR[3:0];
  assign D = ADR;
  assign RS = RX;
  assign WS = RY;
endmodule
