// Digital circuit Mem.dig as structural Verilog
module Mem (
  input  [1:0] RS,
  input  RE,
  input  [1:0] WS,
  input  WE,
  input  CLK,
  input  [7:0] BI,
  output [7:0] BO,
  output [7:0] R0,
  output [7:0] R1,
  output [7:0] R2,
  output [7:0] R3
);

  wire demultiplexer_1_out_0, demultiplexer_1_out_1, demultiplexer_1_out_2, demultiplexer_1_out_3,
       demultiplexer_2_out_0, demultiplexer_2_out_1, demultiplexer_2_out_2, demultiplexer_2_out_3;

  Demultiplexer #(.Selector_Bits(2)) demultiplexer_1 (
    .sel(RS), .in(RE), .out_0(demultiplexer_1_out_0), .out_1(demultiplexer_1_out_1),
    .out_2(demultiplexer_1_out_2), .out_3(demultiplexer_1_out_3));
  Demultiplexer #(.Selector_Bits(2)) demultiplexer_2 (
    .sel(WS), .in(WE), .out_0(demultiplexer_2_out_0), .out_1(demultiplexer_2_out_1),
    .out_2(demultiplexer_2_out_2), .out_3(demultiplexer_2_out_3));
  _3StateBuf _3statebuf_1 (.IN(R0), .EN(demultiplexer_2_out_0), .OUT(BO));
  GodRegister godregister_1 (.RE(demultiplexer_1_out_0), .CLK(CLK), .D(BI), .Q(R0));
  GodRegister godregister_2 (.RE(demultiplexer_1_out_1), .CLK(CLK), .D(BI), .Q(R1));
  _3StateBuf _3statebuf_2 (.IN(R1), .EN(demultiplexer_2_out_1), .OUT(BO));
  _3StateBuf _3statebuf_3 (.IN(R2), .EN(demultiplexer_2_out_2), .OUT(BO));
  GodRegister godregister_3 (.RE(demultiplexer_1_out_2), .CLK(CLK), .D(BI), .Q(R2));
  _3StateBuf _3statebuf_4 (.IN(R3), .EN(demultiplexer_2_out_3), .OUT(BO));
  GodRegister godregister_4 (.RE(demultiplexer_1_out_3), .CLK(CLK), .D(BI), .Q(R3));
endmodule
