// Digital circuit Meths.dig as structural Verilog
module Meths (
  input  [7:0] R1,
  input  [7:0] R2,
  input  [7:0] R3,
  input  [7:0] R4,
  input  [1:0] RSA,
  input  [1:0] RSB,
  input  AW,
  input  AS,
  input  CLK,
  output [7:0] RES,
  output EZ
);

  wire equalszero_1_out;
  wire [7:0] multiplexer_1_out, multiplexer_2_out;

  Multiplexer #(.Selector_Bits(2), .Bits(8)) multiplexer_1 (
    .sel(RSA), .in_0(R1), .in_1(R2), .in_2(R3), .in_3(R4), .out(multiplexer_1_out));
  Multiplexer #(.Selector_Bits(2), .Bits(8)) multiplexer_2 (
    .sel(RSB), .in_0(R1), .in_1(R2), .in_2(R3), .in_3(R4), .out(multiplexer_2_out));
  AdderSubtracter addersubtracter_1 (.A(multiplexer_1_out), .B(multiplexer_2_out), .SUB(AS), .EN(AW), .S(RES));
  D_FF d_ff_1 (.D(equalszero_1_out), .C(CLK), .Q(EZ));  // open: nQ
  EqualsZero equalszero_1 (.IN(RES), .OUT(equalszero_1_out));
endmodule
