// Digital circuit ProgCounter.dig as structural Verilog
module ProgCounter (
  input  HLT,
  input  CLK,
  input  [7:0] D,
  input  DE,
  output [7:0] Q,
  output RC,
  output TC
);

  wire _74191_1_pin11, _74191_2_pin11, _74191_2_pin14, and_1_out, and_2_out, delay_1_out;

  _74191 _74191_1 (
    .pin1(D[1]), .pin2(Q[1]), .pin3(Q[0]), .pin4(HLT), .pin5(1'b0), .pin6(Q[2]), .pin7(Q[3]), .pin8(1'b0),
    .pin9(D[3]), .pin10(D[2]), .pin11(_74191_1_pin11), .pin12(TC), .pin13(RC), .pin14(CLK), .pin15(D[0]),
    .pin16(1'b1));
  _74191 _74191_2 (
    .pin1(D[5]), .pin2(Q[5]), .pin3(Q[4]), .pin4(HLT), .pin5(1'b0), .pin6(Q[6]), .pin7(Q[7]), .pin8(1'b0),
    .pin9(D[7]), .pin10(D[6]), .pin11(_74191_2_pin11), .pin14(_74191_2_pin14), .pin15(D[4]), .pin16(1'b1));  // open: pin12, pin13
  not not_1 (_74191_1_pin11, and_1_out);
  not not_2 (_74191_2_pin14, Q[3]);
  not not_3 (_74191_2_pin11, and_1_out);
  // Probe on and_2_out
  and and_1 (and_1_out, DE, and_2_out);
  and and_2 (and_2_out, CLK, ~delay_1_out);  // And
  Delay #(.delayTime(4)) delay_1 (.in(CLK), .out(delay_1_out));

  // Notes on the sheet:
  //   CLK: Hz: 2
endmodule
