// Digital circuit Prosessar.dig as structural Verilog
module Prosessar (
  input  clk,
  output [7:0] out_2,
  output [7:0] R0,
  output [7:0] R1,
  output [7:0] R2,
  output [7:0] R3,
  output [7:0] out_7,
  output [3:0] out_8,
  output [1:0] out_9,
  output [1:0] out_10,
  output [7:0] out_11
);

  wire delay_1_out, kontrol_1_as, kontrol_1_aw, kontrol_1_ce, kontrol_1_co, kontrol_1_de, kontrol_1_mr,
       kontrol_1_mw, kontrol_1_rr, kontrol_1_rw, meths_1_ez, not_1_out, not_2_out;
  wire [1:0] kontrol_1_aa, kontrol_1_ab, kontrol_1_rs, kontrol_1_ws;
  wire [3:0] kontrol_1_ad;
  wire [7:0] kontrol_1_d;

  not not_1 (not_1_out, clk);
  not not_2 (not_2_out, kontrol_1_ce);
  ProgCounter progcounter_1 (
    .HLT(not_2_out), .CLK(not_1_out), .D(kontrol_1_d), .DE(delay_1_out), .Q(out_7));  // open: RC, TC
  Rohm rohm_1 (.CLK(clk), .ADR(out_7), .INS({out_8, out_9, out_10, out_11}));
  Delay delay_1 (.in(kontrol_1_co), .out(delay_1_out));
  Kontrol kontrol_1 (
    .OP(out_8), .RX(out_9), .RY(out_10), .ADR(out_11), .EZ(meths_1_ez), .MR(kontrol_1_mr), .MW(kontrol_1_mw),
    .RS(kontrol_1_rs), .WS(kontrol_1_ws), .AA(kontrol_1_aa), .AB(kontrol_1_ab), .AS(kontrol_1_as),
    .AW(kontrol_1_aw), .D(kontrol_1_d), .DE(kontrol_1_de), .CE(kontrol_1_ce), .AD(kontrol_1_ad),
    .CO(kontrol_1_co), .RR(kontrol_1_rr), .RW(kontrol_1_rw));
  SerialData serialdata_1 (.D(kontrol_1_d), .DE(kontrol_1_de), .Q(out_2));
  Mem mem_1 (
    .RS(kontrol_1_rs), .RE(kontrol_1_mr), .WS(kontrol_1_ws), .WE(kontrol_1_mw), .CLK(not_1_out), .BI(out_2),
    .BO(out_2), .R0(R0), .R1(R1), .R2(R2), .R3(R3));
  Meths meths_1 (
    .R1(R0), .R2(R1), .R3(R2), .R4(R3), .RSA(kontrol_1_aa), .RSB(kontrol_1_ab), .AW(kontrol_1_aw),
    .AS(kontrol_1_as), .CLK(not_1_out), .RES(out_2), .EZ(meths_1_ez));
  Ryam ryam_1 (.BI(out_2), .ADDR(kontrol_1_ad), .RR(kontrol_1_rr), .RW(kontrol_1_rw), .CLK(not_1_out), .BO(out_2));

  // Notes on the sheet:
  //   clk: Hz: 5
  //   BUS
  //   CLK+
  //   CLK
endmodule
