// Digital circuit Rohm.dig as structural Verilog
module Rohm (
  input  CLK,
  input  [7:0] ADR,
  output [15:0] INS
);

  wire [15:0] rom_1_d;

  ROM #(.bigEndian("true"), .AddrBits(8), .isProgramMemory("true"), .Bits(16)) rom_1 (.A(ADR), .sel(1'b1), .D(rom_1_d));
  Register #(.Bits(16)) INSTR (.D(rom_1_d), .C(CLK), .en(1'b1), .Q(INS));

  // Notes on the sheet:
  //   rom_1 loads main.hex
endmodule
