// Digital circuit Ryam.dig as structural Verilog
module Ryam (
  input  [7:0] BI,
  input  [3:0] ADDR,
  input  RR,
  input  RW,
  input  CLK,
  output [7:0] BO
);

  wire and_1_out, and_2_out, delay_1_out, not_1_out, not_2_out, or_1_out;
  wire [7:0] _74189_1_pin5, not_3_out;

  and and_1 (and_1_out, RR, and_2_out);
  Delay #(.delayTime(4)) delay_1 (.in(CLK), .out(delay_1_out));
  and and_2 (and_2_out, CLK, ~delay_1_out);  // And
  or or_1 (or_1_out, and_1_out, RW);
  not not_1 (not_1_out, or_1_out);
  not not_2 (not_2_out, and_1_out);
  _74189 _74189_1 (
    .pin1(ADDR[0]), .pin2(not_1_out), .pin3(not_2_out), .pin4(BI[0]), .pin5(_74189_1_pin5[0]), .pin6(BI[1]),
    .pin7(_74189_1_pin5[1]), .pin8(1'b0), .pin9(_74189_1_pin5[2]), .pin10(BI[2]), .pin11(_74189_1_pin5[3]),
    .pin12(BI[3]), .pin13(ADDR[3]), .pin14(ADDR[2]), .pin15(ADDR[1]), .pin16(1'b1));
  _74189 _74189_2 (
    .pin1(ADDR[0]), .pin2(not_1_out), .pin3(not_2_out), .pin4(BI[4]), .pin5(_74189_1_pin5[4]), .pin6(BI[5]),
    .pin7(_74189_1_pin5[5]), .pin8(1'b0), .pin9(_74189_1_pin5[6]), .pin10(BI[6]), .pin11(_74189_1_pin5[7]),
    .pin12(BI[7]), .pin13(ADDR[3]), .pin14(ADDR[2]), .pin15(ADDR[1]), .pin16(1'b1));
  assign not_3_out = ~_74189_1_pin5;  // Not not_3, 8 bits wide
  _3StateBuf _3statebuf_1 (.IN(not_3_out), .EN(RW), .OUT(BO));
endmodule
