// Digital circuit SerialData.dig as structural Verilog
module SerialData (
  input  [7:0] D,
  input  DE,
  output [7:0] Q
);

  wire not_1_out;

  not not_1 (not_1_out, DE);
  _74244 _74244_1 (
    .pin1(not_1_out), .pin2(D[0]), .pin3(Q[7]), .pin4(D[1]), .pin5(Q[6]), .pin6(D[2]), .pin7(Q[5]),
    .pin8(D[3]), .pin9(Q[4]), .pin10(1'b0), .pin11(D[4]), .pin12(Q[3]), .pin13(D[5]), .pin14(Q[2]),
    .pin15(D[6]), .pin16(Q[1]), .pin17(D[7]), .pin18(Q[0]), .pin19(not_1_out), .pin20(1'b1));
endmodule
